# Fritzing sketch VintageGauge (saved by Fritzing 0.9.3b)
perfboards: 2

parts:
  Part1 = Arduino Uno (Rev3)  # not connected
  Part2 = Arduino Prototyping Shield
  U1 = Tri-Color LED SMD [package=led-tricolor-smd]  # not connected
  U2 = Tri-Color LED SMD [package=led-tricolor-smd]  # not connected
  U3 = Tri-Color LED SMD [package=led-tricolor-smd]  # not connected
  U4 = Tri-Color LED SMD [package=led-tricolor-smd]  # not connected
  U5 = Tri-Color LED SMD [package=led-tricolor-smd]  # not connected
  U6 = Tri-Color LED SMD [package=led-tricolor-smd]  # not connected
  U7 = Tri-Color LED SMD [package=led-tricolor-smd]  # not connected
  U8 = Tri-Color LED SMD [package=led-tricolor-smd]  # not connected
  U9 = Tri-Color LED SMD [package=led-tricolor-smd]  # not connected
  U10 = Tri-Color LED SMD [package=led-tricolor-smd]  # not connected
  U11 = Tri-Color LED SMD [package=led-tricolor-smd]  # not connected
  U12 = Tri-Color LED SMD [package=led-tricolor-smd]  # not connected
  U13 = Tri-Color LED SMD [package=led-tricolor-smd]  # not connected
  U14 = Tri-Color LED SMD [package=led-tricolor-smd]  # not connected
  U15 = Tri-Color LED SMD [package=led-tricolor-smd]  # not connected
  U16 = Tri-Color LED SMD [package=led-tricolor-smd]  # not connected
  U17 = Tri-Color LED SMD [package=led-tricolor-smd]  # not connected
  U18 = Tri-Color LED SMD [package=led-tricolor-smd]  # not connected
  U19 = Tri-Color LED SMD [package=led-tricolor-smd]  # not connected
  U20 = Tri-Color LED SMD [package=led-tricolor-smd]  # not connected
  U21 = Tri-Color LED SMD [package=led-tricolor-smd]  # not connected
  U22 = Tri-Color LED SMD [package=led-tricolor-smd]  # not connected
  U23 = Tri-Color LED SMD [package=led-tricolor-smd]  # not connected
  U24 = Tri-Color LED SMD [package=led-tricolor-smd]  # not connected
  U25 = Tri-Color LED SMD [package=led-tricolor-smd]  # not connected
  U26 = Tri-Color LED SMD [package=led-tricolor-smd]  # not connected
  U27 = Tri-Color LED SMD [package=led-tricolor-smd]  # not connected
  U28 = Tri-Color LED SMD [package=led-tricolor-smd]  # not connected
  U29 = Tri-Color LED SMD [package=led-tricolor-smd]  # not connected
  U30 = Tri-Color LED SMD [package=led-tricolor-smd]  # not connected
  U31 = Tri-Color LED SMD [package=led-tricolor-smd]  # not connected
  U32 = Tri-Color LED SMD [package=led-tricolor-smd]  # not connected
  Part3 = Breakout Board for Electret Microphone  # not connected
  R1 = Rotary Potentiometer (Small) [maximum_resistance=100kΩ package=THT]  # not connected
  Digital_Panel_Meter_Voltage_DMS-20PC_by_Murata1 = Digital Panel Meter, Voltage, DMS-20PC
  LED1 = LED - 5mm [color="Orange (605nm)" package="5 mm [THT]"]
  R2 = Resistor [tolerance=±5% resistance=220 package=THT]

nets:
  N1: Part2.+5V, Part2.N$276, Part2.N$292, Digital_Panel_Meter_Voltage_DMS-20PC_by_Murata1.6:_#DP1
  N2: Part2.GND, Part2.N$241, Part2.N$263, Part2.N$293, R2.Pin_0
  N3: Part2.N$431, LED1.anode
  N4: LED1.cathode, R2.Pin_1

notes:
  Electret Mic Sensor with trimmer calibration and digital feedback
  4 NeoPixel strips, 8 LEDs
  Analog Milliamperometer
